# Fritzing sketch Card_Reader (saved by Fritzing 0.9.2b)

parts:
  Raspberry_Pi1 = Raspberry Pi 2
  J1 = Piezo Speaker
  LED1 = LED - 5mm [color="Red (633nm)" package="5 mm [THT]"]
  R1 = Resistor [tolerance=±5% resistance=220 package=THT]

nets:
  N1: Raspberry_Pi1.GND, J1.pin1, LED1.cathode
  N2: Raspberry_Pi1.GPIO24, R1.Pin_0
  N3: Raspberry_Pi1.GPIO23, J1.pin2

notes:
  Ground (GND)
  Connects to GND of LED and buzzer
  peg1 = 17
  peg2 = 27
  peg3 = 22
